// Logisim project multiplier.circ as structural Verilog: 1 circuit, main circuit main
module main (
  input  s1,
  input  a,
  input  b,
  input  s2,
  input  c,
  input  d,
  output w,
  output out_8,
  output out_9,
  output out_10,
  output out_11
);

  wire and_2_out, and_3_out, and_4_out, nand_1_out;

  xor xor_1 (w, s1, s2);
  and and_1 (out_8, d, c, b, a);
  and and_2 (and_2_out, c, a);
  nand nand_1 (nand_1_out, d, b);
  and and_3 (and_3_out, d, a);
  and and_4 (and_4_out, c, b);
  and and_5 (out_11, d, b);
  and and_6 (out_9, and_2_out, nand_1_out);
  xor xor_2 (out_10, and_3_out, and_4_out);

  // Notes on the sheet:
  //   x
  //   y
  //   z
endmodule
